# Fritzing sketch 01_digital_io_figure_2 (saved by Fritzing 0.9.3b)
breadboards: 1

parts:
  Part1 = Adafruit Metro M0 Express
  S1 = Toggle Switch [package=THT]

nets:
  N1: Part1.A1, S1.COM
  N2: Part1.3.3V, S1.L2
  N3: Part1.GND, S1.L1

custom parts:
  Adafruit Metro M0 Express: Metro is our series of microcontroller boards for use with the Arduino IDE. This new Metro board looks a whole lot like our original Metro 328, but with a huge upgrade. Instead of the ATmega328, this Metro features a ATSAMD21G18 chip, an ARM Cortex M0+. It's our first Metro that is designed for use with CircuitPython! CircuitPython is our beginner-oriented flavor of MicroPython - and as the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
