# Fritzing sketch 03_i2c_spi_figure_2 (saved by Fritzing 0.9.3b)
breadboards: 1

parts:
  Part1 = Adafruit Metro M0 Express
  Part3 = Adafruit Thermocouple Amplifier MAX31855 [part_number="Adafruit #269"]

nets:
  N1: Part1.MISO, Part3.DO
  N2: Part1.SCK, Part3.CLK
  N3: Part1.D2, Part3.CS
  +5V: Part1.+5V, Part3.VIN
  GND: Part1.GND, Part3.GND

custom parts:
  Adafruit Metro M0 Express: Metro is our series of microcontroller boards for use with the Arduino IDE. This new Metro board looks a whole lot like our original Metro 328, but with a huge upgrade. Instead of the ATmega328, this Metro features a ATSAMD21G18 chip, an ARM Cortex M0+. It's our first Metro that is designed for use with CircuitPython! CircuitPython is our beginner-oriented flavor of MicroPython - and as the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
  Adafruit Thermocouple Amplifier MAX31855: Thermocouples are very sensitive, requiring a good amplifier with a cold-compensation reference. The MAX31855K does everything for you, and can be easily interfaced with any microcontroller, even one without an analog input. This breakout board has the chip itself, a 3.3V regulator with 10uF bypass capacitors and level shifting circuitry, all assembled and tested. Comes with a 2 pin terminal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
